# Fritzing sketch wiring (saved by Fritzing 0.9.5d)
perfboards: 1

parts:
  WeMos_D1_Mini1 = WeMos D1 Mini
  IC1 = ULN2003A [package="DIP16 [THT]"]
  R1 = Resistor [tolerance=±5% resistance=1k package=THT]
  R2 = Resistor [tolerance=±5% resistance=1.2 package=THT]
  R3 = Resistor [tolerance=±5% resistance=1.2 package=THT]
  R4 = Resistor [tolerance=±5% resistance=1M package=THT]
  R5 = Resistor [tolerance=±5% resistance=147 package=THT]
  J1 = screw terminal, 3 pins
  J3 = Terminal Block - 3 pins [package=THT]
  J4 = Terminal Block - 2 pins [package=THT]
  J5 = Terminal Block - 2 pins [package=THT]
  R6 = Resistor [tolerance=±5% resistance=10k package=THT]
  J6 = Terminal Block - 2 pins [package=THT]
  R7 = Resistor [tolerance=±5% resistance=330 package=THT]
  U1 = TSR12450

nets:
  N1: WeMos_D1_Mini1.3V3, R6.Pin_1
  N2: WeMos_D1_Mini1.5V, U1.OUT
  N3: WeMos_D1_Mini1.D0, R1.Pin_0
  N4: WeMos_D1_Mini1.D5, R4.Pin_1, R5.Pin_0
  N5: WeMos_D1_Mini1.D6, J6.Line_2
  N6: WeMos_D1_Mini1.D7, J5.Line_1
  N7: WeMos_D1_Mini1.D8, J4.Line_1
  N8: WeMos_D1_Mini1.G, IC1.0V
  N9: IC1.In_1, R1.Pin_1
  N10: IC1.Out_1, R2.Pin_0, R3.Pin_0
  N11: R2.Pin_1, R3.Pin_1, R4.Pin_0, J3.Line_3
  N12: J1.pin1, J3.Line_2, U1.GND
  N13: J1.pin3, J3.Line_1, U1.IN
  N14: J4.Line_2, J5.Line_2, R6.Pin_0
  N15: J6.Line_1, R7.Pin_0

custom parts:
  Terminal Block - 3 pins: Generic Screw Terminal 9.5mm
  Terminal Block - 2 pins: Generic Screw Terminal 9.5mm
  TSR12450: Mini DC/DC Step-Down (Buck) Converter - 5V @ 1A output - TSR12450
